# Fritzing sketch breadnbutter (saved by Fritzing 1.0.3b)
circuit board: 4.99999cm x 10cm
breadboards: 2

parts:
  S11 = SPST Switch [package=switch-spdt_kit]
  Power_plug2 = Power plug
  4001 = Rectifier Diode [part_number=1N4001 package="300 mil [THT]"]
  100uF = Electrolytic Capacitor [capacitance=0.1mF voltage=35V package="100 mil [THT, electrolytic]"]
  LM7805 = Voltage Regulator [package=to220-igo]
  100uF1 = Electrolytic Capacitor [capacitance=0.1mF voltage=35V package="100 mil [THT, electrolytic]"]
  104 = Ceramic Capacitor [capacitance=100nF voltage=16V package="200 mil [THT, multilayer]"]
  -G = double row female pin header, 4 pins [form="♀ (female)"]
  +v = double row female pin header, 4 pins [form="♀ (female)"]
  +5v = double row female pin header, 4 pins [form="♀ (female)"]
  J4 = double row female pin header, 2 pins [form="♀ (female)"]
  LED2 = LED - 3mm [color="Blue (505nm)" current=0.030A package="3 mm [THT]"]
  1K = Resistor [tolerance=±5% resistance=1k power=0.25W package=THT]
  LED3 = LED - 3mm [color="Blue (505nm)" current=0.030A package="3 mm [THT]"]
  1K_2 = Resistor [tolerance=±5% resistance=1k power=0.25W package=THT]
  IO1 = Audio Jack (TRS) 3.5mm [package="PG203J [THT]"]
  IO1_2 = double row female pin header, 4 pins [form="♀ (female)"]
  LDR = double row female pin header, 4 pins [form="♀ (female)"]
  LED4 = LED - 3mm [color="Red (635nm)" current=0.030A package="3 mm [THT]"]
  1K1 = Resistor [tolerance=±5% resistance=1k power=0.25W package=THT]
  LDR1 = Photocell (LDR) [power=0.25W dark_resistance_@0.01lx=300kΩ light_resistance_@100lx=400Ω luminance=10lx package=THT]
  LED = female pin header, 2 pins [form="♀ (female)"]
  100K = Rotary Potentiometer (Small) [maximum_resistance=100kΩ knob_status=50% power=0.5W package=THT]
  LM324 = LM124-324 Quad Opamp [package="DIP (Dual Inline)"]
  100K_2 = Resistor [tolerance=±5% resistance=100k power=0.25W package=THT]
  Jm2 = double row female pin header, 6 pins [form="♀ (female)"]
  100K7 = Rotary Potentiometer (Small) [maximum_resistance=100kΩ knob_status=50% power=0.5W package=THT]
  100K8 = Rotary Potentiometer (Small) [maximum_resistance=100kΩ knob_status=50% power=0.5W package=THT]
  Jm4 = double row female pin header, 6 pins [form="♀ (female)"]
  100K9 = Rotary Potentiometer (Small) [maximum_resistance=100kΩ knob_status=50% power=0.5W package=THT]
  Jm5 = double row female pin header, 6 pins [form="♀ (female)"]
  Jm6 = double row female pin header, 6 pins [form="♀ (female)"]
  Mix-In = double row female pin header, 6 pins [form="♀ (female)"]
  1uF = Electrolytic Capacitor [capacitance=1µF voltage=35V package="100 mil [THT, electrolytic]"]
  105 = Ceramic Capacitor [capacitance=1µF voltage=16V package="200 mil [THT, multilayer]"]
  100u = Electrolytic Capacitor [capacitance=0.1mF voltage=35V package="100 mil [THT, electrolytic]"]
  out = Audio Jack (TRS) 3.5mm [package="PG203J [THT]"]
  10K = Rotary Potentiometer (Small) [maximum_resistance=10kΩ knob_status=50% power=0.5W package=THT]
  105_2 = Ceramic Capacitor [capacitance=1µF voltage=16V package="200 mil [THT, multilayer]"]
  100K_3 = Resistor [tolerance=±5% resistance=100k power=0.25W package=THT]
  105_3 = Ceramic Capacitor [capacitance=1µF voltage=16V package="200 mil [THT, multilayer]"]
  10K_2 = Resistor [tolerance=±5% resistance=10k power=0.25W package=THT]
  100K_4 = Resistor [tolerance=±5% resistance=100k power=0.25W package=THT]
  100K_5 = Resistor [tolerance=±5% resistance=100k power=0.25W package=THT]
  100K_6 = Resistor [tolerance=±5% resistance=100k power=0.25W package=THT]
  47pf = Ceramic Capacitor [capacitance=47pF voltage=16V package="200 mil [THT, multilayer]"]
  100K_7 = Resistor [tolerance=±5% resistance=100k power=0.25W package=THT]
  100K_8 = Resistor [tolerance=±5% resistance=100k power=0.25W package=THT]
  out_2 = double row female pin header, 2 pins [form="♀ (female)"]
  1K_3 = Resistor [tolerance=±5% resistance=1k power=0.25W package=THT]
  1K_4 = Resistor [tolerance=±5% resistance=1k power=0.25W package=THT]
  100K_9 = Resistor [tolerance=±5% resistance=100k power=0.25W package=THT]
  10K_3 = Resistor [tolerance=±5% resistance=10k power=0.25W package=THT]
  100u1 = Electrolytic Capacitor [capacitance=0.1mF voltage=35V package="100 mil [THT, electrolytic]"]
  104_2 = Ceramic Capacitor [capacitance=100nF voltage=16V package="200 mil [THT, multilayer]"]
  104_3 = Ceramic Capacitor [capacitance=100nF voltage=16V package="200 mil [THT, multilayer]"]
  100 = Resistor [tolerance=±5% resistance=100 power=0.25W package=THT]
  SPKR1 = Loudspeaker
  sw2 = SPST Switch [package=switch-spdt_kit]
  sw1 = SPST Switch [package=switch-spdt_kit]
  sw1_2 = female pin header, 2 pins [form="♀ (female)"]
  sw2_2 = female pin header, 2 pins [form="♀ (female)"]

nets:
  N1: S11.P, Power_plug2.VCC, J4.pin1
  N2: S11.S, 4001.anode
  GND: Power_plug2.GND, 100uF.-, LM7805.GND, 100uF1.-, 104.1, -G.pin1, -G.pin2, -G.pin3, -G.pin4, J4.pin2, 1K.Pin_1, 1K_2.Pin_1, IO1.Sleeve, 1K1.Pin_1, LM324.3IN-, LM324.VCC-, 100u.-, out.Sleeve, 100K_5.Pin_1, 10K_3.Pin_0, 100.Pin_1, SPKR1.pin2
  N3: 4001.cathode, 100uF.+, LM7805.IN, +v.pin1, +v.pin2, +v.pin3, +v.pin4, LED3.anode, LM324.VCC+, 100K_6.Pin_0
  N4: LM7805.OUT, 100uF1.+, 104.0, +5v.pin1, +5v.pin2, +5v.pin3, +5v.pin4, LED2.anode
  N5: LED2.cathode, 1K.Pin_0
  N6: LED3.cathode, 1K_2.Pin_0
  N7: IO1.Ring, IO1_2.pin3, IO1_2.pin4
  N8: IO1.Tip, IO1_2.pin1, IO1_2.pin2
  N9: LDR.pin1, LDR.pin2, LDR1.pin_1
  N10: LDR.pin3, LDR.pin4, LDR1.pin_0
  N11: LED4.cathode, 1K1.Pin_0
  N12: LED4.anode, LED.pin1, LED.pin2
  N13: 100K.leg1, Jm2.pin3, Jm2.pin4
  N14: 100K.wiper, Jm2.pin2, Jm2.pin5
  N15: 100K.leg2, Jm2.pin1, Jm2.pin6
  N16: LM324.1OUT, 10K.leg1, 100K_4.Pin_1, 47pf.0
  N17: LM324.1IN-, 100K_2.Pin_1, 100K_3.Pin_1, 10K_2.Pin_1, 100K_4.Pin_0, 47pf.1
  N18: LM324.1IN+, LM324.2IN+, 100u.+, 10K.wiper, 100K_5.Pin_0, 100K_6.Pin_1
  N19: LM324.2IN-, 100K_7.Pin_0, 100K_8.Pin_1
  N20: LM324.2OUT, 1uF.+, 100K_7.Pin_1
  N21: LM324.3OUT, 100u1.+, 104_3.1
  N22: LM324.3IN+, 100K_9.Pin_0, 10K_3.Pin_1
  N23: 100K_2.Pin_0, 105.0
  N24: 100K7.leg1, Jm6.pin3, Jm6.pin4
  N25: 100K7.wiper, Jm6.pin2, Jm6.pin5
  N26: 100K7.leg2, Jm6.pin1, Jm6.pin6
  N27: 100K8.leg1, Jm4.pin3, Jm4.pin4
  N28: 100K8.wiper, Jm4.pin2, Jm4.pin5
  N29: 100K8.leg2, Jm4.pin1, Jm4.pin6
  N30: 100K9.leg1, Jm5.pin3, Jm5.pin4
  N31: 100K9.wiper, Jm5.pin2, Jm5.pin5
  N32: 100K9.leg2, Jm5.pin1, Jm5.pin6
  N33: Mix-In.pin1, Mix-In.pin6, 105.1
  N34: Mix-In.pin2, Mix-In.pin5, 105_2.1
  N35: Mix-In.pin3, Mix-In.pin4, 105_3.1
  N36: 1uF.-, 1K_3.Pin_1, 1K_4.Pin_1
  N37: out.Ring, out_2.pin2, 1K_4.Pin_0
  N38: out.Tip, out_2.pin1, 1K_3.Pin_0, 100K_9.Pin_1
  N39: 10K.leg2, 100K_8.Pin_0
  N40: 105_2.0, 100K_3.Pin_0
  N41: 105_3.0, 10K_2.Pin_0
  N42: 100u1.-, SPKR1.pin1
  N43: 104_2.0, 100.Pin_0
  N44: 104_2.1, 104_3.0
  N45: sw2.O, sw2_2.pin1
  N46: sw2.P, sw2_2.pin2
  N47: sw1.O, sw1_2.pin1
  N48: sw1.P, sw1_2.pin2

notes:
  10x 1x 1x
  bread'n'butter
